// Logisim project Darkstar.circ as structural Verilog
module ALU (
  input  [2:0] ALU_Op,
  input  ADD0_SUB1_SRL0_SRA1,
  input  [31:0] A,
  input  [31:0] B,
  output L,
  output LU,
  output EQ,
  output NEQ,
  output GE,
  output GEU,
  output [31:0] Res
);

  wire [31:0] adder_1_out, and_1_out, bit_extender_1_out, bit_extender_2_out, multiplexer_1_out,
       multiplexer_2_out, negator_1_out, or_1_out, shifter_1_out, shifter_2_out, shifter_3_out, xor_1_out;

  Negator #(.width(32)) negator_1 (.in(B), .out(negator_1_out));
  Multiplexer #(.width(32)) multiplexer_1 (
    .in0(B), .in1(negator_1_out), .out(multiplexer_1_out), .sel(ADD0_SUB1_SRL0_SRA1));
  Adder #(.width(32)) adder_1 (.a(A), .b(multiplexer_1_out), .out(adder_1_out), .cin(1'b0));  // open: cout
  Shifter #(.width(32)) shifter_1 (.in(A), .\dist (B[4:0]), .out(shifter_1_out));
  Comparator #(.width(32)) comparator_1 (.a(A), .b(B), .eq(EQ), .lt(L));  // open: gt
  Comparator #(.mode("unsigned"), .width(32)) comparator_2 (.a(A), .b(B), .lt(LU));  // open: gt, eq
  Shifter #(.shift("lr"), .width(32)) shifter_2 (.in(A), .\dist (B[4:0]), .out(shifter_2_out));
  Shifter #(.shift("ar"), .width(32)) shifter_3 (.in(A), .\dist (B[4:0]), .out(shifter_3_out));
  assign or_1_out = A | B;  // OR_Gate or_1, 32 bits wide
  assign and_1_out = A & B;  // AND_Gate and_1, 32 bits wide
  assign xor_1_out = A ^ B;  // XOR_Gate xor_1, 32 bits wide
  Multiplexer #(.width(32)) multiplexer_2 (
    .in0(shifter_2_out), .in1(shifter_3_out), .out(multiplexer_2_out), .sel(ADD0_SUB1_SRL0_SRA1));
  assign bit_extender_1_out = {{31{1'b0}}, L};  // Bit_Extender bit_extender_1
  assign bit_extender_2_out = {{31{1'b0}}, LU};  // Bit_Extender bit_extender_2
  not not_1 (NEQ, EQ);
  not not_2 (GE, L);
  not not_3 (GEU, LU);
  Multiplexer #(.select(3), .width(32)) multiplexer_3 (
    .in0(adder_1_out), .in1(shifter_1_out), .in2(bit_extender_1_out), .in3(bit_extender_2_out),
    .in4(xor_1_out), .in5(multiplexer_2_out), .in6(or_1_out), .in7(and_1_out), .out(Res), .sel(ALU_Op));

  // Notes on the sheet:
  //   110 = OR
  //   111 = AND
  //   Opcodes
  //   000 = ADD / SUB
  //   001 = SLL (Shift Left Logical)
  //   010 = SLT (Set if Less Than)
  //   100 = XOR (Exclusive OR)
  //   011 = SLTU (Set if Less Than (Unsigned))
  //   101 = SRL (Shift Right Logical) / SRA (Shift Right Arithmetic)
endmodule

module Regfile (
  input  [4:0] Read_Register1,
  input  [4:0] Read_Register2,
  input  [31:0] Write_Data,
  input  Reset,
  input  [4:0] Write_Register,
  input  Write_Enable,
  input  [31:0] PC_In,
  output [31:0] Reg1_Out,
  output [31:0] Reg2_Out,
  output [31:0] PC_Out
);

  wire clock_1_out, decoder_1_out1, decoder_1_out2, decoder_1_out3, decoder_1_out4, decoder_1_out5,
       decoder_1_out6, decoder_1_out7, decoder_1_out8, decoder_1_out9, decoder_1_out10, decoder_1_out11,
       decoder_1_out12, decoder_1_out13, decoder_1_out14, decoder_1_out15, decoder_1_out16, decoder_1_out17,
       decoder_1_out18, decoder_1_out19, decoder_1_out20, decoder_1_out21, decoder_1_out22, decoder_1_out23,
       decoder_1_out24, decoder_1_out25, decoder_1_out26, decoder_1_out27, decoder_1_out28, decoder_1_out29,
       decoder_1_out30, decoder_1_out31;
  wire [31:0] x0_q, x1_q, x2_q, x3_q, x4_q, x5_q, x6_q, x7_q, x8_q, x9_q, x10_q, x11_q, x12_q, x13_q, x14_q,
       x15_q, x16_q, x17_q, x18_q, x19_q, x20_q, x21_q, x22_q, x23_q, x24_q, x25_q, x26_q, x27_q, x28_q,
       x29_q, x30_q, x31_q;

  Clock clock_1 (.out(clock_1_out));
  Decoder #(.select(5)) decoder_1 (
    .out1(decoder_1_out1), .out2(decoder_1_out2), .out3(decoder_1_out3), .out4(decoder_1_out4),
    .out5(decoder_1_out5), .out6(decoder_1_out6), .out7(decoder_1_out7), .out8(decoder_1_out8),
    .out9(decoder_1_out9), .out10(decoder_1_out10), .out11(decoder_1_out11), .out12(decoder_1_out12),
    .out13(decoder_1_out13), .out14(decoder_1_out14), .out15(decoder_1_out15), .out16(decoder_1_out16),
    .out17(decoder_1_out17), .out18(decoder_1_out18), .out19(decoder_1_out19), .out20(decoder_1_out20),
    .out21(decoder_1_out21), .out22(decoder_1_out22), .out23(decoder_1_out23), .out24(decoder_1_out24),
    .out25(decoder_1_out25), .out26(decoder_1_out26), .out27(decoder_1_out27), .out28(decoder_1_out28),
    .out29(decoder_1_out29), .out30(decoder_1_out30), .out31(decoder_1_out31), .sel(Write_Register),
    .en(Write_Enable));  // open: out0
  Register #(.width(32)) x0 (.D(Write_Data), .en(1'b0), .clk(clock_1_out), .Q(x0_q), .clr(Reset));
  Register #(.width(32)) x1 (.D(Write_Data), .en(decoder_1_out1), .clk(clock_1_out), .Q(x1_q), .clr(Reset));
  Register #(.width(32)) x2 (.D(Write_Data), .en(decoder_1_out2), .clk(clock_1_out), .Q(x2_q), .clr(Reset));
  Register #(.width(32)) x3 (.D(Write_Data), .en(decoder_1_out3), .clk(clock_1_out), .Q(x3_q), .clr(Reset));
  Register #(.width(32)) x4 (.D(Write_Data), .en(decoder_1_out4), .clk(clock_1_out), .Q(x4_q), .clr(Reset));
  Register #(.width(32)) x5 (.D(Write_Data), .en(decoder_1_out5), .clk(clock_1_out), .Q(x5_q), .clr(Reset));
  Register #(.width(32)) x6 (.D(Write_Data), .en(decoder_1_out6), .clk(clock_1_out), .Q(x6_q), .clr(Reset));
  Register #(.width(32)) x7 (.D(Write_Data), .en(decoder_1_out7), .clk(clock_1_out), .Q(x7_q), .clr(Reset));
  Register #(.width(32)) x8 (.D(Write_Data), .en(decoder_1_out8), .clk(clock_1_out), .Q(x8_q), .clr(Reset));
  Register #(.width(32)) x9 (.D(Write_Data), .en(decoder_1_out9), .clk(clock_1_out), .Q(x9_q), .clr(Reset));
  Register #(.width(32)) x10 (.D(Write_Data), .en(decoder_1_out10), .clk(clock_1_out), .Q(x10_q), .clr(Reset));
  Register #(.width(32)) x11 (.D(Write_Data), .en(decoder_1_out11), .clk(clock_1_out), .Q(x11_q), .clr(Reset));
  Register #(.width(32)) x12 (.D(Write_Data), .en(decoder_1_out12), .clk(clock_1_out), .Q(x12_q), .clr(Reset));
  Register #(.width(32)) x13 (.D(Write_Data), .en(decoder_1_out13), .clk(clock_1_out), .Q(x13_q), .clr(Reset));
  Register #(.width(32)) x14 (.D(Write_Data), .en(decoder_1_out14), .clk(clock_1_out), .Q(x14_q), .clr(Reset));
  Register #(.width(32)) x15 (.D(Write_Data), .en(decoder_1_out15), .clk(clock_1_out), .Q(x15_q), .clr(Reset));
  Register #(.width(32)) x16 (.D(Write_Data), .en(decoder_1_out16), .clk(clock_1_out), .Q(x16_q), .clr(Reset));
  Register #(.width(32)) x17 (.D(Write_Data), .en(decoder_1_out17), .clk(clock_1_out), .Q(x17_q), .clr(Reset));
  Register #(.width(32)) x18 (.D(Write_Data), .en(decoder_1_out18), .clk(clock_1_out), .Q(x18_q), .clr(Reset));
  Register #(.width(32)) x19 (.D(Write_Data), .en(decoder_1_out19), .clk(clock_1_out), .Q(x19_q), .clr(Reset));
  Register #(.width(32)) x20 (.D(Write_Data), .en(decoder_1_out20), .clk(clock_1_out), .Q(x20_q), .clr(Reset));
  Register #(.width(32)) x21 (.D(Write_Data), .en(decoder_1_out21), .clk(clock_1_out), .Q(x21_q), .clr(Reset));
  Register #(.width(32)) x22 (.D(Write_Data), .en(decoder_1_out22), .clk(clock_1_out), .Q(x22_q), .clr(Reset));
  Register #(.width(32)) x23 (.D(Write_Data), .en(decoder_1_out23), .clk(clock_1_out), .Q(x23_q), .clr(Reset));
  Register #(.width(32)) x24 (.D(Write_Data), .en(decoder_1_out24), .clk(clock_1_out), .Q(x24_q), .clr(Reset));
  Register #(.width(32)) x25 (.D(Write_Data), .en(decoder_1_out25), .clk(clock_1_out), .Q(x25_q), .clr(Reset));
  Register #(.width(32)) x26 (.D(Write_Data), .en(decoder_1_out26), .clk(clock_1_out), .Q(x26_q), .clr(Reset));
  Register #(.width(32)) x27 (.D(Write_Data), .en(decoder_1_out27), .clk(clock_1_out), .Q(x27_q), .clr(Reset));
  Register #(.width(32)) x28 (.D(Write_Data), .en(decoder_1_out28), .clk(clock_1_out), .Q(x28_q), .clr(Reset));
  Register #(.width(32)) x29 (.D(Write_Data), .en(decoder_1_out29), .clk(clock_1_out), .Q(x29_q), .clr(Reset));
  Register #(.width(32)) x30 (.D(Write_Data), .en(decoder_1_out30), .clk(clock_1_out), .Q(x30_q), .clr(Reset));
  Register #(.width(32)) x31 (.D(Write_Data), .en(decoder_1_out31), .clk(clock_1_out), .Q(x31_q), .clr(Reset));
  Register #(.width(32)) pc (.D(PC_In), .en(1'b1), .clk(clock_1_out), .Q(PC_Out), .clr(Reset));
  Multiplexer #(.select(5), .width(32)) multiplexer_1 (
    .in0(x0_q), .in1(x1_q), .in2(x2_q), .in3(x3_q), .in4(x4_q), .in5(x5_q), .in6(x6_q), .in7(x7_q),
    .in8(x8_q), .in9(x9_q), .in10(x10_q), .in11(x11_q), .in12(x12_q), .in13(x13_q), .in14(x14_q),
    .in15(x15_q), .in16(x16_q), .in17(x17_q), .in18(x18_q), .in19(x19_q), .in20(x20_q), .in21(x21_q),
    .in22(x22_q), .in23(x23_q), .in24(x24_q), .in25(x25_q), .in26(x26_q), .in27(x27_q), .in28(x28_q),
    .in29(x29_q), .in30(x30_q), .in31(x31_q), .out(Reg1_Out), .sel(Read_Register1));
  Multiplexer #(.select(5), .width(32)) multiplexer_2 (
    .in0(x0_q), .in1(x1_q), .in2(x2_q), .in3(x3_q), .in4(x4_q), .in5(x5_q), .in6(x6_q), .in7(x7_q),
    .in8(x8_q), .in9(x9_q), .in10(x10_q), .in11(x11_q), .in12(x12_q), .in13(x13_q), .in14(x14_q),
    .in15(x15_q), .in16(x16_q), .in17(x17_q), .in18(x18_q), .in19(x19_q), .in20(x20_q), .in21(x21_q),
    .in22(x22_q), .in23(x23_q), .in24(x24_q), .in25(x25_q), .in26(x26_q), .in27(x27_q), .in28(x28_q),
    .in29(x29_q), .in30(x30_q), .in31(x31_q), .out(Reg2_Out), .sel(Read_Register2));
endmodule
